# Fritzing sketch RPi.DHT (saved by Fritzing 0.9.2b)

parts:
  DHT1 = DHT22 Humidity and Temperature Sensor
  Raspberry_Pi_B_rev1 = Raspberry Pi B rev1

nets:
  VDD: DHT1.VDD, Raspberry_Pi_B_rev1.3V3
  N1: DHT1.DATA, Raspberry_Pi_B_rev1.GPIO_21
  GND: DHT1.GND, Raspberry_Pi_B_rev1.GND
